# Fritzing sketch Alarma láser IoT en fritzing (saved by Fritzing 0.9.3b)
breadboards: 1

parts:
  INTRUSION = LED - 5mm [color="Red (635nm)" package="5 mm [THT]"]
  ON/OFF = Pushbutton [package="[THT]"]
  R5 = Resistor [tolerance=±5% resistance=1k package=THT]
  EMISOR = KY-008 Laser Transmitter Module [package="Breakout board"]
  ACTIVADO = LED - 5mm [color="Green (565nm)" package="5 mm [THT]"]
  R6 = Resistor [tolerance=±5% resistance=220 package=THT]
  MODULO_STEP_DOWN = LM2596 step down module
  RECEPTOR = laser receiver [package=THT]
  R8 = Resistor [tolerance=±5% resistance=220 package=THT]
  NodeMCU = ESP8266 NodeMCU LoLin module
  PANEL_SOLAR = Solar Panel [package="Renogy 50 Watts 12 Volt Monocrystalline Bendable Solar Panel"]
  Q1 = TRANSISTOR_NPN [package=to-92-ammo]
  D1 = Rectifier Diode [part_number=1N4001 package="300 mil [THT]"]
  R9 = Resistor [tolerance=±5% resistance=1k package=THT]
  RELÈ_2_CANAL = 2-Channel 5v Relay Shield [package=relay-2ch5v10a]
  SIRENA = Piezo Speaker

nets:
  GND: INTRUSION.cathode, R5.Pin_0, ACTIVADO.cathode, MODULO_STEP_DOWN.IN-, MODULO_STEP_DOWN.OUT-, NodeMCU.GND, PANEL_SOLAR.Connector_2, RELÈ_2_CANAL.GND
  N1: INTRUSION.anode, R8.Pin_0
  N2: ON/OFF.Pin_1, ON/OFF.Pin_2, R5.Pin_1, NodeMCU.D8
  N3: ON/OFF.Pin_3, ON/OFF.Pin_4, MODULO_STEP_DOWN.OUT+, NodeMCU.Vin, D1.cathode, SIRENA.pin2
  N4: EMISOR.S, NodeMCU.D5
  N5: EMISOR.-, RECEPTOR.pin1, Q1.E
  N6: ACTIVADO.anode, R6.Pin_0
  N7: R6.Pin_1, NodeMCU.D0
  N8: MODULO_STEP_DOWN.IN+, PANEL_SOLAR.Connector_1, RELÈ_2_CANAL.VCC
  N9: RECEPTOR.pin2, NodeMCU.D1
  N10: R8.Pin_1, NodeMCU.D4
  N11: NodeMCU.D2, R9.Pin_0
  N12: NodeMCU.D6, RELÈ_2_CANAL.IN1
  N13: NodeMCU.D7, RELÈ_2_CANAL.IN2
  N14: Q1.B, R9.Pin_1
  N15: Q1.C, D1.anode, SIRENA.pin1

custom parts:
  KY-008 Laser Transmitter Module: KY-008 Laser Transmitter Module, emits a dot shaped red laser beam.
  LM2596 step down module: LM2596 DC-DC step down power supply module 3 A.
  laser receiver: Generic non modulated laser receiver module.
  ESP8266 NodeMCU LoLin module: ESP8266 based NodeMCU
  Solar Panel: Renogy 50 Watts 12 Volt Solar Panel
  2-Channel 5v Relay Shield: 2 Channel 5v Relay Shield w. 2x SPD-06VDC-SD-C
